# Fritzing sketch Circuit A frtiz (saved by Fritzing 0.9.4)
breadboards: 1

parts:
  U1 = SN74LS21N [package="DIP14 [THT]"]
  U4 = SN74LS14N [package="DIP14 [THT]"]
  U5 = 4071 4 x 2 Input OR Gate, multi-part [part_number=4071 package="DIP (Dual Inline) [THT]"]

nets:
  N1: U1.1B, U4.1Y
  N2: U1.NC#2, U5.connector0
  N3: U1.1C, U4.1A
  N4: U1.1Y, U5.connector1
  GND: U1.GND, U4.GND, U5.connector6
  VCC: U1.VCC, U4.VCC, U5.connector13

notes:
  Input A
  Input B
  Input C
  Output Z
