# Fritzing sketch Circuit DIagram (saved by Fritzing 0.9.4)
breadboards: 4

parts:
  U1 = PCF8574 [package="DIP16 [THT]"]
  U4 = 74HC4052 [package=dil16]
  U5 = 4011 4 x 2 Input NAND Gate, multi-part [part_number=4011 package="DIP (Dual Inline) [THT]"]
  U5_1 = 4011_4_x_2_input_NAND_gate_multipart_subpart2 [part_number=4011]  # not connected
  U5_2 = 4011_4_x_2_input_NAND_gate_multipart_subpart3 [part_number=4011]  # not connected
  SW1 = DIP Switch 8 Position [package=dipswitch-08]
  SW2 = DIP Switch 8 Position [package=dipswitch-08]
  U2 = PCF8574 [package="DIP16 [THT]"]
  U7 = 4001 4 x 2 Input NOR Gate, single part [part_number=4001 package="DIP (Dual Inline) [THT]"]
  U8 = 4077 4 x 2 Input XNOR Gate, multi-part [part_number=4077 package="DIP (Dual Inline) [THT]"]
  U8_1 = 4077_4_x_2_input_XNOR_gate_multipart_subpart2 [part_number=4077]  # not connected
  U8_2 = 4077_4_x_2_input_XNOR_gate_multipart_subpart3 [part_number=4077]  # not connected
  U9 = 74HC04_HEX_INVERTER [package=dil14]
  U10 = 74HC4052 [package=dil16]
  U11 = 74HC4052 [package=dil16]
  U12 = 74HC4052 [package=dil16]
  U14 = 74HC4052 [package=dil16]
  U15 = 74HC4052 [package=dil16]
  U16 = 4077 4 x 2 Input XNOR Gate, multi-part [part_number=4077 package="DIP (Dual Inline) [THT]"]
  U16_1 = 4077_4_x_2_input_XNOR_gate_multipart_subpart2 [part_number=4077]  # not connected

nets:
  N1: U1.A0, SW1.5
  N2: U1.A1, SW1.6
  N3: U1.A2, SW1.7
  N4: U1.P0, SW1.8
  N5: U1.P1, U11.VCC
  N6: U1.P2, U2.P3, U12.Y1
  N7: U1.INT, U5.connector0, U7.B1, U8.connector1
  N8: U4.Y0, U5.connector5
  N9: U4.Y2, U7.B2
  N10: U4.Y, U8.connector5
  N11: U4.X2, U10.Y2
  N12: U4.VCC, U10.Y0
  N13: U5.connector1, U2.INT, U7.A1, U8.connector0
  N14: U5.connector2, U5.connector3, U5.connector4
  N15: SW1.1, U2.A0
  N16: SW1.2, U2.A1
  N17: SW1.3, U2.A2
  N18: SW1.4, U2.P0
  N19: SW2.2, U10.GND
  N20: SW2.3, U11.GND
  N21: SW2.4, U11.VEE
  N22: SW2.5, U11.INH
  N23: SW2.7, U16.connector0
  N24: U2.P1, U11.X2
  N25: U7.Q1, U7.Q2, U7.A2
  N26: U8.connector2, U8.connector3, U8.connector4
  N27: U9.1A, U10.VCC
  N28: U9.1Y, U11.Y0
  N29: U10.X2, U11.Y2
  N30: U12.Y0, U12.X1, U15.Y2
  N31: U12.Y3, U16.connector2
  N32: U12.X2, U15.Y0
  N33: U14.Y0, U15.Y3
  N34: U14.Y, U16.connector1

notes:
  Routing
  Computational
  FlipFlop
  Counter
  3-Input NAND
  Control Unit

// code stored in the sketch: Lab2 Circuit.ino

